// Logisim project ejemplo1Arqui73.circ as structural Verilog: 9 circuits, main circuit main
module main (
  input  A,
  input  B,
  input  C,
  input  D
);

  wire modulo_7seg_1_sa, modulo_7seg_1_sb, modulo_7seg_1_sc, modulo_7seg_1_sd, modulo_7seg_1_se,
       modulo_7seg_1_sf, modulo_7seg_1_sg;

  modulo_7seg modulo_7seg_1 (
    .A(A), .B(B), .C(C), .D(D), .SA(modulo_7seg_1_sa), .SB(modulo_7seg_1_sb), .SC(modulo_7seg_1_sc),
    .SD(modulo_7seg_1_sd), .SE(modulo_7seg_1_se), .SF(modulo_7seg_1_sf), .SG(modulo_7seg_1_sg));
  _7_Segment_Display u_7_segment_display_1 (
    .g(modulo_7seg_1_sg), .f(modulo_7seg_1_sf), .a(modulo_7seg_1_sa), .b(modulo_7seg_1_sb),
    .e(modulo_7seg_1_se), .d(modulo_7seg_1_sd), .c(modulo_7seg_1_sc));  // open: dp
endmodule

module seg_A (
  input  A,
  input  B,
  input  C,
  input  D,
  output SA
);

  wire and_1_out, and_2_out, not_1_out, not_2_out;

  not not_1 (not_1_out, B);
  and and_1 (and_1_out, not_1_out, not_2_out);
  not not_2 (not_2_out, D);
  and and_2 (and_2_out, B, D);
  or or_1 (SA, A, and_1_out, and_2_out, C);
endmodule

module seg_B (
  input  A,
  input  B,
  input  C,
  input  D,
  output SB
);

  wire and_1_out, and_2_out, not_1_out, not_2_out, not_3_out, or_1_out;

  not not_1 (not_1_out, B);
  not not_2 (not_2_out, C);
  not not_3 (not_3_out, D);
  and and_1 (and_1_out, not_2_out, not_3_out);
  or or_1 (or_1_out, not_1_out, and_1_out);
  and and_2 (and_2_out, C, D);
  or or_2 (SB, or_1_out, and_2_out);
endmodule

module seg_C (
  input  A,
  input  B,
  input  C,
  input  D,
  output SC
);

  wire not_1_out, or_1_out;

  not not_1 (not_1_out, C);
  or or_1 (or_1_out, not_1_out, D);
  or or_2 (SC, or_1_out, B);
endmodule

module seg_D (
  input  A,
  input  B,
  input  C,
  input  D,
  output SD
);

  wire and_1_out, and_2_out, and_3_out, and_4_out, not_1_out, not_2_out, not_3_out;

  not not_1 (not_1_out, B);
  not not_2 (not_2_out, C);
  not not_3 (not_3_out, D);
  and and_1 (and_1_out, not_1_out, not_3_out);
  and and_2 (and_2_out, not_1_out, C);
  and and_3 (and_3_out, B, not_2_out, D);
  and and_4 (and_4_out, C, not_3_out);
  or or_1 (SD, and_1_out, and_2_out, and_3_out, and_4_out, A);
endmodule

module seg_E (
  input  A,
  input  B,
  input  C,
  input  D,
  output SE
);

  wire and_1_out, and_2_out, not_1_out, not_2_out;

  not not_1 (not_1_out, B);
  not not_2 (not_2_out, D);
  and and_1 (and_1_out, C, not_2_out);
  and and_2 (and_2_out, not_1_out, not_2_out);
  or or_1 (SE, and_2_out, and_1_out);
endmodule

module seg_F (
  input  A,
  input  B,
  input  C,
  input  D,
  output SF
);

  wire and_1_out, and_2_out, and_3_out, not_1_out, not_2_out, or_1_out, or_2_out;

  not not_1 (not_1_out, C);
  not not_2 (not_2_out, D);
  and and_1 (and_1_out, not_1_out, not_2_out);
  and and_2 (and_2_out, B, not_1_out);
  and and_3 (and_3_out, B, not_2_out);
  or or_1 (or_1_out, and_1_out, and_2_out);
  or or_2 (or_2_out, and_3_out, A);
  or or_3 (SF, or_1_out, or_2_out);
endmodule

module seg_G (
  input  A,
  input  B,
  input  C,
  input  D,
  output SG
);

  wire and_1_out, and_2_out, and_3_out, not_1_out, not_2_out, not_3_out, or_1_out, or_2_out;

  not not_1 (not_1_out, B);
  not not_2 (not_2_out, C);
  not not_3 (not_3_out, D);
  and and_1 (and_1_out, not_1_out, C);
  and and_2 (and_2_out, not_2_out, B);
  and and_3 (and_3_out, C, not_3_out);
  or or_1 (or_1_out, and_1_out, and_2_out);
  or or_2 (or_2_out, A, and_3_out);
  or or_3 (SG, or_1_out, or_2_out);
endmodule

module modulo_7seg (
  input  A,
  input  B,
  input  C,
  input  D,
  output SA,
  output SB,
  output SC,
  output SD,
  output SE,
  output SF,
  output SG
);

  seg_A seg_a_1 (.A(A), .B(B), .C(C), .D(D), .SA(SA));
  seg_B seg_b_1 (.A(A), .B(B), .C(C), .D(D), .SB(SB));
  seg_C seg_c_1 (.A(A), .B(B), .C(C), .D(D), .SC(SC));
  seg_D seg_d_1 (.A(A), .B(B), .C(C), .D(D), .SD(SD));
  seg_E seg_e_1 (.A(A), .B(B), .C(C), .D(D), .SE(SE));
  seg_F seg_f_1 (.A(A), .B(B), .C(C), .D(D), .SF(SF));
  seg_G seg_g_1 (.A(A), .B(B), .C(C), .D(D), .SG(SG));
endmodule
